# Fritzing sketch tempSensor (saved by Fritzing 0.9.3b)
perfboards: 1

parts:
  Raspberry_Pi_1 = Raspberry Pi 3 [part_number=RPI-3-V1.2]
  DS3 = DS18B20 1-Wire Temperature Sensor [part_number=DS18B20]
  R1 = Resistor [tolerance=±5% resistance=10k package="0402 [SMD]"]  # not connected
  J6 = female pin header, 3 pins [form="♀ (female)"]
  J7 = male pin header, 5 pins [form="♂ (male)"]  # not connected
  J8 = single row smd male pin header, 5 pins [form="♂ (male)"]  # not connected
  J9 = male pin header, 5 pins [form="♂ (male)"]  # not connected
  J10 = female pin header, 3 pins [form="♀ (female)"]  # not connected
  J11 = female alternating pin header, 3 pins [form="♀ (female)"]
  IC1 = IC, DIP package, 16 pins [chip_label=MCP3424]
  IC2 = IC, DIP package, 10 pins [chip_label=FCL100-1]
  IC3 = IC, DIP package, 10 pins [chip_label=FCL100-2]
  IC4 = IC, DIP package, 10 pins [chip_label=FCL100-3]

nets:
  N1: Raspberry_Pi_1.3v3, J11.pin1
  N2: Raspberry_Pi_1.GPIO3, IC1.pin5
  N3: Raspberry_Pi_1.GPIO4, J11.pin2
  N4: Raspberry_Pi_1.GND, J11.pin3, IC1.pin6, IC2.pin1, IC3.pin1
  N5: Raspberry_Pi_1.5V, IC2.pin2, IC3.pin2, IC4.pin2
  N6: DS3.GND, J6.pin1
  N7: DS3.DQ, J6.pin2
  N8: DS3.VDD, J6.pin3
  N9: IC1.pin11, IC4.pin4
  N10: IC1.pin12, IC4.pin5
  N11: IC1.pin13, IC3.pin5
  N12: IC1.pin14, IC3.pin4
  N13: IC1.pin15, IC2.pin5
  N14: IC1.pin16, IC2.pin4
  N15: IC2.pin3, IC3.pin3, IC4.pin3

notes:
  4 x temp probe,
  Connect to board
  For MOS ICs VDD is the more positive supply voltage and Vss is the more negative supply voltage.
  connect FCL100 sync
